# Fritzing sketch guitarANDsnake_Conections (saved by Fritzing 0.9.3b)
breadboards: 2

parts:
  Componente3 = Arduino Uno (Rev3)
  Componente4 = Matrix LED de 8x8 basada en MAX7219
  LED3 = smd LED [color="Red (633nm)" package="0805 [SMD]"]
  U4 = LCD-16X2 [package=lcd-16x2_noholes]
  R11 = Resistor [tolerance=±5% resistance=220 package=THT]
  R12 = Resistor [tolerance=±5% resistance=220 package=THT]
  R13 = Resistor [tolerance=±5% resistance=220 package=THT]
  R14 = Resistor [tolerance=±5% resistance=220 package=THT]
  R15 = Resistor [tolerance=±5% resistance=220 package=THT]
  S5 = Pushbutton [package="[SMD]"]
  S6 = Pushbutton [package="[SMD]"]
  S7 = Pushbutton [package="[SMD]"]
  S8 = Pushbutton [package="[SMD]"]
  J2 = Piezo Speaker
  SG3 = Buzzer 12mm [part_number=1 package=buzzer-12mm-ns]
  SG4 = Buzzer 12mm [package=buzzer-12mm-ns]
  R16 = Resistor [tolerance=±5% resistance=220 package=THT]
  R17 = Resistor [tolerance=±5% resistance=220 package=THT]
  LED4 = smd LED [color="Green (555nm)" package="0805 [SMD]"]

nets:
  N1: Componente3.A0, R12.Pin_1, S6.Pin_3, S6.Pin_4
  N2: Componente3.A1, R17.Pin_1
  N3: Componente3.A2, R16.Pin_1
  N4: Componente3.A3, SG4.2
  N5: Componente3.A4/SDA, SG3.2
  N6: Componente3.A5/SCL, J2.pin2
  N7: Componente3.D8, U4.DB7
  N8: Componente3.D9_PWM, U4.DB6
  N9: Componente3.D10_PWM/SS, U4.DB5
  N10: Componente3.D11_PWM/MOSI, U4.DB4
  N11: Componente3.D12/MISO, U4.E
  N12: Componente3.D13/SCK, U4.RS
  GND: Componente3.GND, Componente4.GND, LED3.cathode, U4.VSS, U4.VO, U4.R_W, U4.K, S5.Pin_1, S5.Pin_2, S6.Pin_1, S6.Pin_2, S7.Pin_1, S7.Pin_2, S8.Pin_1, S8.Pin_2, J2.pin1, SG3.1, SG4.1, LED4.cathode
  N13: Componente3.D2, Componente4.DIN
  N14: Componente3.D3_PWM, Componente4.CS
  N15: Componente3.D4, Componente4.CLK
  N16: Componente3.D5_PWM, R11.Pin_1, S5.Pin_3, S5.Pin_4
  N17: Componente3.D6_PWM, R13.Pin_1, S7.Pin_3, S7.Pin_4
  N18: Componente3.D7, R14.Pin_1, S8.Pin_3, S8.Pin_4
  5V: Componente3.5V, Componente4.VCC, U4.VDD, R11.Pin_0, R12.Pin_0, R13.Pin_0, R14.Pin_0, R15.Pin_0
  N19: LED3.anode, R17.Pin_0
  N20: U4.A, R15.Pin_1
  N21: R16.Pin_0, LED4.anode

notes:
  Buzzer 1
  A4
  LED Verde
  A2
  220ohm
  LED Verme
  A1
  220ohm
  LEGENDA
  PRETO GND
  VERMELHO 5V
  CIANO MATRIZ
  VERDE LCD
  CONTROLE (220ohm)
  1 - BRANCO (ESQUERDA) 5
  2 - ROSA (CIMA) A0
  3 - AZUL (BAIXO) 6
  4 - LARANJA (DIREITA) 7
  LCD
  1 GND
  2 5V
  3 GND
  4 13
  5 GND
  6 12
  11 11
  12 10
  13 9
  14 8
  15 5V (220ohms)
  16 GND
  Speaker
  A5
  Buzer 2
  A3
  MATRIZ
  VCC 5V
  GND GND
  DIN 2
  CS 3
  CLK 4
